// Logisim project projeto1_arquitetura.circ as structural Verilog: 5 circuits, main circuit main
module main (
  input  A0,
  input  A1,
  input  A2,
  input  A3,
  input  Ci,
  input  B0,
  input  B1,
  input  B2,
  input  B3,
  output S0,
  output S1,
  output S2,
  output S3,
  output Overflow,
  output C0
);

  wire decodificador_1_a_2, decodificador_1_b_2, decodificador_1_c_2, decodificador_1_d_2, decodificador_1_e,
       decodificador_1_f, decodificador_1_g, decodificador_2_a_2, decodificador_2_b_2, decodificador_2_c_2,
       decodificador_2_d_2, decodificador_2_e, decodificador_2_f, decodificador_2_g, decodificador_3_a_2,
       decodificador_3_b_2, decodificador_3_c_2, decodificador_3_d_2, decodificador_3_e, decodificador_3_f,
       decodificador_3_g;

  Decodificador decodificador_1 (
    .A(A3), .B(A2), .C(A1), .D(A0), .a_2(decodificador_1_a_2), .b_2(decodificador_1_b_2),
    .c_2(decodificador_1_c_2), .d_2(decodificador_1_d_2), .e(decodificador_1_e), .f(decodificador_1_f),
    .g(decodificador_1_g));
  somador_4_bits somador_4_bits_1 (
    .Ci0(Ci), .A0(A0), .B0(B0), .A1(A1), .B1(B1), .A2(A2), .B2(B2), .A3(A3), .B3(B3), .C03(C0),
    .Overflow(Overflow), .S0(S0), .S1(S1), .S2(S2), .S3(S3));
  Decodificador decodificador_2 (
    .A(B2), .B(B1), .C(B3), .D(B0), .a_2(decodificador_2_a_2), .b_2(decodificador_2_b_2),
    .c_2(decodificador_2_c_2), .d_2(decodificador_2_d_2), .e(decodificador_2_e), .f(decodificador_2_f),
    .g(decodificador_2_g));
  _7_Segment_Display u_7_segment_display_1 (
    .g(decodificador_1_g), .f(decodificador_1_f), .a(decodificador_1_a_2), .b(decodificador_1_b_2),
    .e(decodificador_1_e), .d(decodificador_1_d_2), .c(decodificador_1_c_2));  // open: dp
  _7_Segment_Display u_7_segment_display_2 (
    .g(decodificador_2_g), .f(decodificador_2_f), .a(decodificador_2_a_2), .b(decodificador_2_b_2),
    .e(decodificador_2_e), .d(decodificador_2_d_2), .c(decodificador_2_c_2));  // open: dp
  Decodificador decodificador_3 (
    .A(S0), .B(S1), .C(S2), .D(S3), .a_2(decodificador_3_a_2), .b_2(decodificador_3_b_2),
    .c_2(decodificador_3_c_2), .d_2(decodificador_3_d_2), .e(decodificador_3_e), .f(decodificador_3_f),
    .g(decodificador_3_g));
  _7_Segment_Display u_7_segment_display_3 (
    .g(decodificador_3_g), .f(decodificador_3_f), .a(decodificador_3_a_2), .b(decodificador_3_b_2),
    .e(decodificador_3_e), .d(decodificador_3_d_2), .c(decodificador_3_c_2));  // open: dp
endmodule

module meia_soma (
  input  A,
  input  B,
  output Soma,
  output Carry_out
);

  xor xor_1 (Soma, A, B);
  and and_1 (Carry_out, A, B);
endmodule

module Somador_completo (
  input  Ci0,
  input  A,
  input  B,
  output S0,
  output C0
);

  wire meia_soma_1_carry_out, meia_soma_1_soma, meia_soma_2_carry_out;

  meia_soma meia_soma_1 (.A(A), .B(B), .Soma(meia_soma_1_soma), .Carry_out(meia_soma_1_carry_out));
  meia_soma meia_soma_2 (.A(meia_soma_1_soma), .B(Ci0), .Soma(S0), .Carry_out(meia_soma_2_carry_out));
  or or_1 (C0, meia_soma_1_carry_out, meia_soma_2_carry_out);
endmodule

module somador_4_bits (
  input  Ci0,
  input  A0,
  input  B0,
  input  A1,
  input  B1,
  input  A2,
  input  B2,
  input  A3,
  input  B3,
  output S0,
  output S1,
  output S2,
  output S3,
  output C03,
  output Overflow
);

  wire somador_completo_1_c0, somador_completo_2_c0, somador_completo_3_c0;

  Somador_completo somador_completo_1 (.A(A0), .B(B0), .Ci0(Ci0), .S0(S0), .C0(somador_completo_1_c0));
  Somador_completo somador_completo_2 (
    .A(A1), .B(B1), .Ci0(somador_completo_1_c0), .S0(S1), .C0(somador_completo_2_c0));
  Somador_completo somador_completo_3 (
    .A(A2), .B(B2), .Ci0(somador_completo_2_c0), .S0(S2), .C0(somador_completo_3_c0));
  Somador_completo somador_completo_4 (.A(A3), .B(B3), .Ci0(somador_completo_3_c0), .S0(S3), .C0(C03));
  xor xor_1 (Overflow, C03, somador_completo_3_c0);
endmodule

module Decodificador (
  input  A,
  input  B,
  input  C,
  input  D,
  output a_2,
  output b_2,
  output c_2,
  output d_2,
  output e,
  output f,
  output g
);

  wire and_1_out, and_2_out, and_3_out, and_4_out, and_5_out, and_6_out, and_7_out, and_8_out, and_9_out,
       and_10_out, and_11_out, and_12_out, and_13_out, and_14_out, and_15_out, and_16_out, and_17_out,
       and_18_out, and_19_out, and_20_out, and_21_out, and_22_out, and_23_out, and_24_out, and_25_out,
       and_26_out, and_27_out, and_28_out, and_29_out, and_30_out, and_31_out, and_32_out, and_33_out,
       and_34_out, and_35_out, not_1_out, not_2_out, not_3_out, not_4_out, not_5_out, not_6_out, not_7_out,
       not_8_out, not_9_out, not_10_out, not_11_out, not_12_out, not_13_out, not_14_out, not_15_out,
       not_16_out, not_17_out, not_18_out, not_19_out, not_20_out, not_21_out, not_22_out, not_23_out,
       not_24_out, not_25_out, not_26_out, not_27_out, not_28_out, not_29_out, not_30_out, not_31_out,
       not_32_out, not_33_out, not_34_out, not_35_out, not_36_out, not_37_out, not_38_out, not_39_out,
       not_40_out, not_41_out, not_42_out, not_43_out;

  not not_1 (not_1_out, B);
  and and_1 (and_1_out, not_1_out, not_2_out);
  not not_2 (not_2_out, D);
  not not_3 (not_3_out, A);
  and and_2 (and_2_out, not_3_out, C);
  not not_4 (not_4_out, A);
  and and_3 (and_3_out, not_4_out, B, D);
  and and_4 (and_4_out, B, C);
  and and_5 (and_5_out, A, not_5_out, not_6_out);
  not not_5 (not_5_out, B);
  not not_6 (not_6_out, C);
  and and_6 (and_6_out, A, not_7_out);
  not not_7 (not_7_out, D);
  not not_8 (not_8_out, A);
  and and_7 (and_7_out, not_8_out, not_9_out);
  not not_9 (not_9_out, B);
  not not_10 (not_10_out, A);
  not not_11 (not_11_out, C);
  and and_8 (and_8_out, not_10_out, not_11_out, not_12_out);
  not not_12 (not_12_out, D);
  not not_13 (not_13_out, B);
  and and_9 (and_9_out, not_13_out, not_14_out);
  not not_14 (not_14_out, D);
  not not_15 (not_15_out, A);
  and and_10 (and_10_out, not_15_out, C, D);
  not not_16 (not_16_out, C);
  and and_11 (and_11_out, A, not_16_out, D);
  not not_17 (not_17_out, A);
  and and_12 (and_12_out, not_17_out, not_18_out);
  not not_18 (not_18_out, C);
  not not_19 (not_19_out, A);
  and and_13 (and_13_out, not_19_out, D);
  not not_20 (not_20_out, C);
  and and_14 (and_14_out, not_20_out, D);
  not not_21 (not_21_out, A);
  and and_15 (and_15_out, not_21_out, B);
  and and_16 (and_16_out, A, not_22_out);
  not not_22 (not_22_out, B);
  not not_23 (not_23_out, A);
  and and_17 (and_17_out, not_23_out, not_24_out, not_25_out);
  not not_24 (not_24_out, B);
  not not_25 (not_25_out, D);
  not not_26 (not_26_out, B);
  and and_18 (and_18_out, not_26_out, C, D);
  not not_27 (not_27_out, C);
  and and_19 (and_19_out, B, not_27_out, D);
  and and_20 (and_20_out, B, C, not_28_out);
  not not_28 (not_28_out, D);
  and and_21 (and_21_out, A, not_29_out);
  not not_29 (not_29_out, C);
  not not_30 (not_30_out, B);
  and and_22 (and_22_out, not_30_out, not_31_out);
  not not_31 (not_31_out, D);
  and and_23 (and_23_out, C, not_32_out);
  not not_32 (not_32_out, D);
  and and_24 (and_24_out, A, C);
  and and_25 (and_25_out, A, B);
  not not_33 (not_33_out, C);
  and and_26 (and_26_out, not_33_out, not_34_out);
  not not_34 (not_34_out, D);
  not not_35 (not_35_out, A);
  and and_27 (and_27_out, not_35_out, B, not_36_out);
  not not_36 (not_36_out, C);
  and and_28 (and_28_out, B, not_37_out);
  not not_37 (not_37_out, D);
  and and_29 (and_29_out, A, not_38_out);
  not not_38 (not_38_out, B);
  and and_30 (and_30_out, A, C);
  not not_39 (not_39_out, B);
  and and_31 (and_31_out, not_39_out, C);
  and and_32 (and_32_out, C, not_40_out);
  not not_40 (not_40_out, D);
  not not_41 (not_41_out, A);
  and and_33 (and_33_out, not_41_out, B, not_42_out);
  not not_42 (not_42_out, C);
  and and_34 (and_34_out, A, not_43_out);
  not not_43 (not_43_out, B);
  and and_35 (and_35_out, A, D);
  or or_1 (b_2, and_7_out, and_8_out, and_9_out, and_10_out, and_11_out);
  or or_2 (c_2, and_12_out, and_13_out, and_14_out, and_15_out, and_16_out);
  or or_3 (d_2, and_17_out, and_18_out, and_19_out, and_20_out, and_21_out);
  or or_4 (e, and_22_out, and_23_out, and_24_out, and_25_out);
  or or_5 (f, and_26_out, and_27_out, and_28_out, and_29_out, and_30_out);
  or or_6 (g, and_31_out, and_32_out, and_33_out, and_34_out, and_35_out);
  or or_7 (a_2, and_1_out, and_2_out, and_3_out, and_4_out, and_5_out, and_6_out);
endmodule
